# Fritzing sketch ArduiWake (saved by Fritzing 0.9.2b)
breadboards: 2

parts:
  Composant1 = Arduino Mega 2560 (Rev3)
  S1 = Pushbutton [package="[SMD]"]
  S2 = Pushbutton [package="[SMD]"]
  S3 = Pushbutton [package="[SMD]"]
  R1 = Resistor [tolerance=±5% resistance=10k package="0603 [SMD]"]
  R2 = Resistor [tolerance=±5% resistance=10k package="0603 [SMD]"]
  R3 = Resistor [tolerance=±5% resistance=10k package="0603 [SMD]"]
  LED1 = smd LED [color="Red (633nm)" package="0603 [SMD]"]
  LED2 = smd LED [color="Yellow (592nm)" package="0603 [SMD]"]
  R4 = Resistor [tolerance=±5% resistance=150 package="0603 [SMD]"]
  R5 = Resistor [tolerance=±5% resistance=150 package="0603 [SMD]"]
  R7 = Rotary Potentiometer (Large) [maximum_resistance=100kΩ package=THT]
  J1 = Piezo Speaker
  LED3 = smd LED [color="Yellow (592nm)" package="0603 [SMD]"]
  R8 = Resistor [tolerance=±5% resistance=150 package="0603 [SMD]"]

nets:
  N1: Composant1.A15, R7.wiper
  N2: Composant1.D18/TX1, S1.Pin_1, S1.Pin_2, R2.Pin_0
  N3: Composant1.D9_PWM, J1.pin2
  N4: Composant1.5V, R1.Pin_1, R2.Pin_1, R3.Pin_1, R7.leg2
  N5: Composant1.GND, Composant1.D28, Composant1.D29, Composant1.D31, S1.Pin_3, S1.Pin_4, S2.Pin_3, S2.Pin_4, S3.Pin_3, S3.Pin_4, LED1.anode, LED2.anode, R7.leg1, J1.pin1, LED3.anode
  N6: Composant1.D24, R8.Pin_0
  N7: Composant1.D25, R4.Pin_0
  N8: Composant1.D27, R5.Pin_0
  N9: S2.Pin_1, S2.Pin_2, R1.Pin_0
  N10: S3.Pin_1, S3.Pin_2, R3.Pin_0
  N11: LED1.cathode, R5.Pin_1
  N12: LED2.cathode, R4.Pin_1
  N13: LED3.cathode, R8.Pin_1
